# Fritzing sketch modbus-ctrl-v1 (saved by Fritzing 0.9.3b)
breadboards: 1

parts:
  T1 = LM35 Temperature Sensor [package="TO92 [THT]"]
  WeMos_D1_Mini_Relay_Shield2 = WeMos D1 Mini Relay Shield
  WeMos_D1_Mini_Relay_Shield3 = WeMos D1 Mini Relay Shield
  WeMos_D1_Mini_Relay_Shield1 = WeMos D1 Mini Relay Shield
  WeMos_D1_Mini_Relay_Shield4 = WeMos D1 Mini Relay Shield
  WeMos_D1_Mini_Relay_Shield5 = WeMos D1 Mini Relay Shield
  S1 = Toggle Switch [package=THT]
  S2 = Toggle Switch [package=THT]
  S3 = Toggle Switch [package=THT]
  S4 = Toggle Switch [package=THT]
  S5 = Toggle Switch [package=THT]
  Часть1 = Arduino Pro Mini v13
  T2 = LM35 Temperature Sensor [package="TO92 [THT]"]
  Component1 = RS485-Modul-Shield

nets:
  N1: T1.Vout, Часть1.A0
  N2: WeMos_D1_Mini_Relay_Shield2.D1, Часть1.D5_PWM
  N3: WeMos_D1_Mini_Relay_Shield3.D1, Часть1.D4
  N4: WeMos_D1_Mini_Relay_Shield1.D1, Часть1.D6_PWM
  N5: WeMos_D1_Mini_Relay_Shield4.D1, Часть1.D3_PWM
  N6: WeMos_D1_Mini_Relay_Shield5.D1, Часть1.D7
  N7: S1.L1, Часть1.D8
  N8: S2.L1, Часть1.D9_PWM
  N9: S3.L1, Часть1.D10_PWM/SS
  N10: S4.L1, Часть1.D11_PWM/MOSI
  N11: S5.L1, Часть1.D12/MISO
  N12: Часть1.A1, T2.Vout
  N13: Часть1.D2, Component1.RE, Component1.DE
  N14: Часть1.D1/RX, Component1.RO
  N15: Часть1.D0/TX, Component1.DI

custom parts:
  RS485-Modul-Shield: Commercially available RS485 to RS232 TTL Module
